// Logisim project M32.circ as structural Verilog
module PC (
  input  [31:0] INPT,
  input  WR,
  output [31:0] OUTPT
);

  wire CLK_out;
  wire [31:0] register_1_q;

  Clock CLK (.out(CLK_out));
  Register #(.width(32)) register_1 (.D(INPT), .en(WR), .clk(CLK_out), .Q(register_1_q));  // open: clr
  Multiplexer #(.width(32)) multiplexer_1 (.in0({32{1'b0}}), .in1(register_1_q), .out(OUTPT));  // open: sel

  // Notes on the sheet:
  //   Programar gnd_vcc
endmodule

module RBANK (
  input  [4:0] S1,
  input  [4:0] S2,
  input  CLK,
  input  [31:0] Rd,
  output [31:0] out_5,
  output [31:0] out_6
);

  wire [31:0] register_1_q, register_2_q, register_3_q, register_4_q, register_5_q, register_6_q,
       register_7_q, register_8_q, register_9_q, register_10_q, register_11_q, register_12_q, register_13_q,
       register_14_q, register_15_q, register_16_q, register_17_q, register_18_q, register_19_q,
       register_20_q, register_21_q, register_22_q, register_23_q, register_24_q, register_25_q,
       register_26_q, register_27_q, register_28_q, register_29_q, register_30_q, register_31_q,
       register_32_q;

  Register #(.width(32)) register_1 (.D(Rd), .Q(register_1_q));  // open: en, clk, clr
  Register #(.width(32)) register_2 (.D(Rd), .Q(register_2_q));  // open: en, clk, clr
  Register #(.width(32)) register_3 (.D(Rd), .Q(register_3_q));  // open: en, clk, clr
  Register #(.width(32)) register_4 (.D(Rd), .Q(register_4_q));  // open: en, clk, clr
  Register #(.width(32)) register_5 (.D(Rd), .Q(register_5_q));  // open: en, clk, clr
  Register #(.width(32)) register_6 (.D(Rd), .Q(register_6_q));  // open: en, clk, clr
  Register #(.width(32)) register_7 (.D(Rd), .Q(register_7_q));  // open: en, clk, clr
  Register #(.width(32)) register_8 (.D(Rd), .Q(register_8_q));  // open: en, clk, clr
  Register #(.width(32)) register_9 (.D(Rd), .Q(register_9_q));  // open: en, clk, clr
  Register #(.width(32)) register_10 (.D(Rd), .Q(register_10_q));  // open: en, clk, clr
  Register #(.width(32)) register_11 (.D(Rd), .Q(register_11_q));  // open: en, clk, clr
  Register #(.width(32)) register_12 (.D(Rd), .Q(register_12_q));  // open: en, clk, clr
  Register #(.width(32)) register_13 (.D(Rd), .Q(register_13_q));  // open: en, clk, clr
  Register #(.width(32)) register_14 (.D(Rd), .Q(register_14_q));  // open: en, clk, clr
  Register #(.width(32)) register_15 (.D(Rd), .Q(register_15_q));  // open: en, clk, clr
  Register #(.width(32)) register_16 (.D(Rd), .Q(register_16_q));  // open: en, clk, clr
  Register #(.width(32)) register_17 (.D(Rd), .Q(register_17_q));  // open: en, clk, clr
  Register #(.width(32)) register_18 (.D(Rd), .Q(register_18_q));  // open: en, clk, clr
  Register #(.width(32)) register_19 (.D(Rd), .Q(register_19_q));  // open: en, clk, clr
  Register #(.width(32)) register_20 (.D(Rd), .Q(register_20_q));  // open: en, clk, clr
  Register #(.width(32)) register_21 (.D(Rd), .Q(register_21_q));  // open: en, clk, clr
  Register #(.width(32)) register_22 (.D(Rd), .Q(register_22_q));  // open: en, clk, clr
  Register #(.width(32)) register_23 (.D(Rd), .Q(register_23_q));  // open: en, clk, clr
  Register #(.width(32)) register_24 (.D(Rd), .Q(register_24_q));  // open: en, clk, clr
  Register #(.width(32)) register_25 (.D(Rd), .Q(register_25_q));  // open: en, clk, clr
  Register #(.width(32)) register_26 (.D(Rd), .Q(register_26_q));  // open: en, clk, clr
  Register #(.width(32)) register_27 (.D(Rd), .Q(register_27_q));  // open: en, clk, clr
  Register #(.width(32)) register_28 (.D(Rd), .Q(register_28_q));  // open: en, clk, clr
  Register #(.width(32)) register_29 (.D(Rd), .clk(CLK), .Q(register_29_q));  // open: en, clr
  Register #(.width(32)) register_30 (.D(Rd), .clk(CLK), .Q(register_30_q));  // open: en, clr
  Register #(.width(32)) register_31 (.D(Rd), .clk(CLK), .Q(register_31_q));  // open: en, clr
  Register #(.width(32)) register_32 (.D(Rd), .clk(CLK), .Q(register_32_q));  // open: en, clr
  Multiplexer #(.select(5), .width(32)) multiplexer_1 (
    .in0(register_1_q), .in1(register_2_q), .in2(register_3_q), .in3(register_4_q), .in4(register_5_q),
    .in5(register_6_q), .in6(register_7_q), .in7(register_8_q), .in8(register_9_q), .in9(register_10_q),
    .in10(register_11_q), .in11(register_12_q), .in12(register_13_q), .in13(register_14_q),
    .in14(register_15_q), .in15(register_16_q), .in16(register_17_q), .in17(register_18_q),
    .in18(register_19_q), .in19(register_20_q), .in20(register_21_q), .in21(register_22_q),
    .in22(register_23_q), .in23(register_24_q), .in24(register_25_q), .in25(register_26_q),
    .in26(register_27_q), .in27(register_28_q), .in28(register_29_q), .in29(register_30_q),
    .in30(register_31_q), .in31(register_32_q), .out(out_5), .sel(S1));
  Multiplexer #(.select(5), .width(32)) multiplexer_2 (
    .in0(register_1_q), .in1(register_2_q), .in2(register_3_q), .in3(register_4_q), .in4(register_5_q),
    .in5(register_6_q), .in6(register_7_q), .in7(register_8_q), .in8(register_9_q), .in9(register_10_q),
    .in10(register_11_q), .in11(register_12_q), .in12(register_13_q), .in13(register_14_q),
    .in14(register_15_q), .in15(register_16_q), .in16(register_17_q), .in17(register_18_q),
    .in18(register_19_q), .in19(register_20_q), .in20(register_21_q), .in21(register_22_q),
    .in22(register_23_q), .in23(register_24_q), .in24(register_25_q), .in25(register_26_q),
    .in26(register_27_q), .in27(register_28_q), .in28(register_29_q), .in29(register_30_q),
    .in30(register_31_q), .in31(register_32_q), .out(out_6), .sel(S2));
endmodule
